# Fritzing sketch pi-adc-phat (saved by Fritzing 0.9.3b)
breadboards: 1

parts:
  OLED_I2C1 = OLED 128x64 I2C Monochrome Display
  IC1 = IC, DIP package, 8 pins [chip_label=3002]
  R1 = Resistor [tolerance=±5% resistance=15k package=THT]
  R2 = Resistor [tolerance=±5% resistance=15k package=THT]
  R3 = Resistor [tolerance=±5% resistance=10k package=THT]
  R4 = Resistor [tolerance=±5% resistance=10k package=THT]
  J1 = male pin header, 2 pins [form="♂ (male)"]
  J2 = male pin header, 2 pins [form="♂ (male)"]
  S1 = Pushbutton [package=THT]
  LED1 = LED - 3mm [color="Green (570nm)" package="3 mm [THT]"]
  R5 = Resistor [tolerance=±5% resistance=100 package=THT]

nets:
  N1: OLED_I2C1.VDD, IC1.pin8
  N2: OLED_I2C1.GND, IC1.pin4, R1.Pin_1, R2.Pin_1, J1.pin1, J1.pin2, S1.leg0, R5.Pin_0
  N3: IC1.pin2, R1.Pin_0, R4.Pin_1
  N4: IC1.pin3, R2.Pin_0, R3.Pin_1
  N5: R3.Pin_0, J2.pin2
  N6: R4.Pin_0, J2.pin1
  N7: LED1.cathode, R5.Pin_1
